// Logisim project ulalib.circ as structural Verilog
module GD (
  input  D,
  input  nE,
  output nQ,
  output Q
);

  wire nor_1_out, nor_3_out;

  nor nor_1 (nor_1_out, D, nE);
  nor nor_2 (Q, nor_1_out, nQ);
  nor nor_3 (nor_3_out, nor_1_out, nE);
  nor nor_4 (nQ, Q, nor_3_out);

  // Notes on the sheet:
  //   r
  //   RS FF
  //   s
endmodule
